// Logisim project 512 bit HPFPU.circ as structural Verilog: 1 circuit, main circuit main
module main (
);

  wire and_1_out, and_2_out, and_3_out, and_4_out, and_5_out, and_6_out, and_7_out, and_8_out, and_9_out,
       and_10_out, and_11_out, and_12_out, and_13_out, and_14_out, and_15_out, and_16_out, and_17_out,
       and_18_out, and_19_out, and_20_out, and_21_out, and_22_out, and_23_out, and_24_out, and_25_out,
       and_26_out, and_27_out, and_28_out, and_29_out, and_30_out, and_31_out, and_32_out, button_1_out,
       button_2_out, dipswitch_3_sw8, dipswitch_6_sw8, nor_1_out, nor_2_out, nor_3_out, nor_4_out, not_1_out,
       not_2_out, not_3_out, not_4_out, not_5_out, not_6_out, not_7_out, not_8_out, not_9_out, not_10_out,
       not_11_out, not_12_out, not_13_out, not_14_out, not_15_out, not_16_out, not_17_out, not_18_out,
       not_19_out, not_20_out, or_1_out, or_2_out, or_6_out, or_7_out, shift_register_1_p11,
       shift_register_1_p12, shift_register_1_p13, shift_register_1_p14, shift_register_1_p15, xor_1_out,
       xor_2_out, xor_3_out, xor_4_out, xor_5_out, xor_6_out, xor_7_out, xor_8_out;
  wire [15:0] dipswitch_1_sw1, dipswitch_4_sw1, register_1_q, register_2_q;
  wire [15:6] shift_register_1_p1;

  DipSwitch dipswitch_1 (
    .sw1(dipswitch_1_sw1[0]), .sw2(dipswitch_1_sw1[1]), .sw3(dipswitch_1_sw1[2]), .sw4(dipswitch_1_sw1[3]),
    .sw5(dipswitch_1_sw1[4]), .sw6(dipswitch_1_sw1[5]));  // open: sw7, sw8
  DipSwitch dipswitch_2 (
    .sw1(dipswitch_1_sw1[6]), .sw2(dipswitch_1_sw1[7]), .sw3(dipswitch_1_sw1[8]), .sw4(dipswitch_1_sw1[9]),
    .sw5(dipswitch_1_sw1[10]), .sw6(dipswitch_1_sw1[11]), .sw7(dipswitch_1_sw1[12]), .sw8(dipswitch_1_sw1[13]));
  DipSwitch dipswitch_3 (
    .sw1(dipswitch_1_sw1[14]), .sw2(dipswitch_1_sw1[15]), .sw8(dipswitch_3_sw8));  // open: sw3, sw4, sw5, sw6, sw7
  Register #(.width(16)) register_1 (
    .D(dipswitch_1_sw1), .en(dipswitch_3_sw8), .clk(button_1_out), .Q(register_1_q));  // open: clr
  Button button_1 (.out(button_1_out));
  not not_1 (not_1_out, register_1_q[1]);
  not not_2 (not_2_out, register_1_q[2]);
  not not_3 (not_3_out, register_1_q[3]);
  not not_4 (not_4_out, register_1_q[4]);
  not not_5 (not_5_out, register_1_q[5]);
  // Shift_Register #(.length(10)) shift_register_1: pin names not known; wires that end beside it: shift_register_1_p1[6], shift_register_1_p1[7], shift_register_1_p1[8], shift_register_1_p1[9], shift_register_1_p1[10], shift_register_1_p1[11], shift_register_1_p1[12], shift_register_1_p1[13], shift_register_1_p1[14], shift_register_1_p1[15], shift_register_1_p11, shift_register_1_p12, shift_register_1_p13, shift_register_1_p14, shift_register_1_p15
  DipSwitch dipswitch_4 (
    .sw1(dipswitch_4_sw1[0]), .sw2(dipswitch_4_sw1[1]), .sw3(dipswitch_4_sw1[2]), .sw4(dipswitch_4_sw1[3]),
    .sw5(dipswitch_4_sw1[4]), .sw6(dipswitch_4_sw1[5]));  // open: sw7, sw8
  xor xor_1 (xor_1_out, register_1_q[1], register_2_q[5]);
  and and_1 (and_1_out, 1'b0, not_6_out);
  not not_6 (not_6_out, xor_1_out);
  and and_2 (and_2_out, not_1_out, register_2_q[5]);
  xor xor_2 (xor_2_out, register_1_q[2], register_2_q[4]);
  and and_3 (and_3_out, or_1_out, not_7_out);
  not not_7 (not_7_out, xor_2_out);
  and and_4 (and_4_out, not_2_out, register_2_q[4]);
  xor xor_3 (xor_3_out, register_1_q[3], register_2_q[3]);
  and and_5 (and_5_out, or_2_out, not_8_out);
  not not_8 (not_8_out, xor_3_out);
  and and_6 (and_6_out, not_3_out, register_2_q[3]);
  xor xor_4 (xor_4_out, register_1_q[4], register_2_q[2]);
  and and_7 (and_7_out, shift_register_1_p11, not_9_out);
  not not_9 (not_9_out, xor_4_out);
  and and_8 (and_8_out, not_4_out, register_2_q[2]);
  xor xor_5 (xor_5_out, register_1_q[5], register_2_q[1]);
  and and_9 (and_9_out, shift_register_1_p13, not_10_out);
  not not_10 (not_10_out, xor_5_out);
  and and_10 (and_10_out, not_5_out, register_2_q[1]);
  DipSwitch dipswitch_5 (
    .sw1(dipswitch_4_sw1[6]), .sw2(dipswitch_4_sw1[7]), .sw3(dipswitch_4_sw1[8]), .sw4(dipswitch_4_sw1[9]),
    .sw5(dipswitch_4_sw1[10]), .sw6(dipswitch_4_sw1[11]), .sw7(dipswitch_4_sw1[12]), .sw8(dipswitch_4_sw1[13]));
  xor xor_6 (xor_6_out, xor_1_out, 1'b0);
  or or_1 (or_1_out, and_1_out, and_2_out);
  xor xor_7 (xor_7_out, xor_2_out, or_1_out);
  or or_2 (or_2_out, and_3_out, and_4_out);
  xor xor_8 (xor_8_out, xor_3_out, or_2_out);
  or or_3 (shift_register_1_p11, and_5_out, and_6_out);
  xor xor_9 (shift_register_1_p12, xor_4_out, shift_register_1_p11);
  or or_4 (shift_register_1_p13, and_7_out, and_8_out);
  xor xor_10 (shift_register_1_p14, xor_5_out, shift_register_1_p13);
  or or_5 (shift_register_1_p15, and_9_out, and_10_out);
  DipSwitch dipswitch_6 (
    .sw1(dipswitch_4_sw1[14]), .sw2(dipswitch_4_sw1[15]), .sw8(dipswitch_6_sw8));  // open: sw3, sw4, sw5, sw6, sw7
  Register #(.width(16)) register_2 (
    .D(dipswitch_4_sw1), .en(dipswitch_6_sw8), .clk(button_2_out), .Q(register_2_q));  // open: clr
  Button button_2 (.out(button_2_out));
  not not_11 (not_11_out, register_1_q[5]);
  not not_12 (not_12_out, register_2_q[1]);
  not not_13 (not_13_out, register_1_q[4]);
  not not_14 (not_14_out, register_2_q[2]);
  not not_15 (not_15_out, register_1_q[3]);
  not not_16 (not_16_out, register_2_q[3]);
  not not_17 (not_17_out, register_1_q[2]);
  not not_18 (not_18_out, register_2_q[4]);
  not not_19 (not_19_out, register_1_q[1]);
  not not_20 (not_20_out, register_2_q[5]);
  and and_11 (and_11_out, not_11_out, register_2_q[1]);
  nor nor_1 (nor_1_out, and_11_out, and_12_out);
  and and_12 (and_12_out, register_1_q[5], not_12_out);
  and and_13 (and_13_out, not_13_out, register_2_q[2]);
  nor nor_2 (nor_2_out, and_13_out, and_14_out);
  and and_14 (and_14_out, register_1_q[4], not_14_out);
  and and_15 (and_15_out, not_15_out, register_2_q[3]);
  nor nor_3 (nor_3_out, and_15_out, and_16_out);
  and and_16 (and_16_out, register_1_q[3], not_16_out);
  and and_17 (and_17_out, not_17_out, register_2_q[4]);
  nor nor_4 (nor_4_out, and_17_out, and_18_out);
  and and_18 (and_18_out, register_1_q[2], not_18_out);
  and and_19 (and_19_out, not_19_out, register_2_q[5]);
  and and_20 (and_20_out, register_1_q[1], not_20_out);
  // Shift_Register #(.length(10)) shift_register_2: pin names not known
  and and_21 (and_21_out, nor_1_out, and_13_out);
  and and_22 (and_22_out, nor_1_out, and_14_out);
  and and_23 (and_23_out, nor_1_out, nor_2_out);
  and and_24 (and_24_out, nor_1_out, nor_2_out);
  and and_25 (and_25_out, nor_1_out, nor_2_out, nor_3_out, and_17_out);
  and and_26 (and_26_out, nor_1_out, nor_2_out, nor_3_out, and_18_out);
  and and_27 (and_27_out, nor_1_out, nor_2_out, nor_3_out, nor_4_out);
  and and_28 (and_28_out, nor_1_out, nor_2_out, nor_3_out, nor_4_out);
  and and_29 (and_29_out, and_23_out, and_15_out);
  and and_30 (and_30_out, and_24_out, and_16_out);
  and and_31 (and_31_out, and_27_out, and_19_out);
  and and_32 (and_32_out, and_28_out, and_20_out);
  or or_6 (or_6_out, and_11_out, and_21_out, and_29_out, and_25_out);
  or or_7 (or_7_out, and_12_out, and_22_out, and_30_out, and_26_out);
  // OR_Gate or_8 has open pins: in0=or_6_out, in1=and_31_out, out=open
  // OR_Gate or_9 has open pins: in0=or_7_out, in1=and_32_out, out=open
  Counter counter_1 ();  // open: load, D, count, Q, carry, clk, clr

  // Notes on the sheet:
  //   Sign & Exponent
  //   Mantissa
  //   Float A
  //   Sign & Exponent
  //   Mantissa
  //   Float B
endmodule
