// Logisim project ALU.circ as structural Verilog: 2 circuits, main circuit main
module main (
  input  in_1
);

  wire button_1_out, dipswitch_1_sw1, dipswitch_1_sw2, dipswitch_1_sw3, not_1_out, R1_Register_A_sw1,
       R1_Register_A_sw2, R1_Register_A_sw3, R1_Register_A_sw4, R1_Register_A_sw5, R1_Register_A_sw6,
       R1_Register_A_sw7, R1_Register_A_sw8, R2_Register_B_sw1, R2_Register_B_sw2, R2_Register_B_sw3,
       R2_Register_B_sw4, R2_Register_B_sw5, R2_Register_B_sw6, R2_Register_B_sw7, R2_Register_B_sw8,
       R3_Control_Signals_sw1, tsb_1_o0, tsb_1_o1, tsb_1_o2, tsb_1_o3, tsb_1_o4, tsb_1_o5, tsb_1_o6,
       tsb_1_o6_2;
  wire [7:0] adder_1_out, nor_1_out, register_1_q, register_2_q, subtractor_1_out, transistor_1_out,
       tsb_2_o0, tsb_3_o0;

  DotMatrix #(.matrixcols(8), .matrixrows(1)) dotmatrix_1 (
    .col0(register_1_q[7]), .col1(register_1_q[6]), .col2(register_1_q[5]), .col3(register_1_q[4]),
    .col4(register_1_q[3]), .col5(register_1_q[2]), .col6(register_1_q[1]), .col7(register_1_q[0]));
  DotMatrix #(.matrixcols(8), .matrixrows(1)) dotmatrix_2 (
    .col0(tsb_1_o6_2), .col1(tsb_1_o6), .col2(tsb_1_o5), .col3(tsb_1_o4), .col4(tsb_1_o3), .col5(tsb_1_o2),
    .col6(tsb_1_o1), .col7(tsb_1_o0));
  DipSwitch R1_Register_A (
    .sw1(R1_Register_A_sw1), .sw2(R1_Register_A_sw2), .sw3(R1_Register_A_sw3), .sw4(R1_Register_A_sw4),
    .sw5(R1_Register_A_sw5), .sw6(R1_Register_A_sw6), .sw7(R1_Register_A_sw7), .sw8(R1_Register_A_sw8));
  DipSwitch R2_Register_B (
    .sw1(R2_Register_B_sw1), .sw2(R2_Register_B_sw2), .sw3(R2_Register_B_sw3), .sw4(R2_Register_B_sw4),
    .sw5(R2_Register_B_sw5), .sw6(R2_Register_B_sw6), .sw7(R2_Register_B_sw7), .sw8(R2_Register_B_sw8));
  DipSwitch dipswitch_1 (
    .sw1(dipswitch_1_sw1), .sw2(dipswitch_1_sw2), .sw3(dipswitch_1_sw3));  // open: sw4, sw5, sw6, sw7, sw8
  Button button_1 (.out(button_1_out));
  DipSwitch R3_Control_Signals (.sw1(R3_Control_Signals_sw1));  // open: sw2, sw3, sw4, sw5, sw6, sw7, sw8
  TSB tsb_1 (
    .OUT(dipswitch_1_sw3), .O0(tsb_1_o0), .O1(tsb_1_o1), .O2(tsb_1_o2), .O3(tsb_1_o3), .O4(tsb_1_o4),
    .O5(tsb_1_o5), .O6(tsb_1_o6), .O6_2(tsb_1_o6_2), .I0(register_2_q[0]), .I1(register_2_q[1]),
    .I2(register_2_q[2]), .I3(register_2_q[3]), .I4(register_2_q[4]), .I5(register_2_q[5]),
    .I6(register_2_q[6]), .I7(register_2_q[7]));  // open: OUT_2
  TSB tsb_2 (
    .O0(tsb_2_o0[0]), .O1(tsb_2_o0[1]), .O2(tsb_2_o0[2]), .O3(tsb_2_o0[3]), .O4(tsb_2_o0[4]),
    .O5(tsb_2_o0[5]), .O6(tsb_2_o0[6]), .O6_2(tsb_2_o0[7]), .I0(R1_Register_A_sw8), .I1(R1_Register_A_sw7),
    .I2(R1_Register_A_sw6), .I3(R1_Register_A_sw5), .I4(R1_Register_A_sw4), .I5(R1_Register_A_sw3),
    .I6(R1_Register_A_sw2), .I7(R1_Register_A_sw1), .OUT_2(dipswitch_1_sw1));  // open: OUT
  TSB tsb_3 (
    .O0(tsb_3_o0[0]), .O1(tsb_3_o0[1]), .O2(tsb_3_o0[2]), .O3(tsb_3_o0[3]), .O4(tsb_3_o0[4]),
    .O5(tsb_3_o0[5]), .O6(tsb_3_o0[6]), .O6_2(tsb_3_o0[7]), .I0(R2_Register_B_sw8), .I1(R2_Register_B_sw7),
    .I2(R2_Register_B_sw6), .I3(R2_Register_B_sw5), .I4(R2_Register_B_sw4), .I5(R2_Register_B_sw3),
    .I6(R2_Register_B_sw2), .I7(R2_Register_B_sw1), .OUT_2(dipswitch_1_sw2));  // open: OUT
  nor nor_1 (nor_1_out[0], register_2_q[7], register_2_q[6], register_2_q[5], register_2_q[4], register_2_q[3], register_2_q[2], register_2_q[1], register_2_q[0]);
  Transistor #(.\type ("n"), .width(8)) transistor_1 (.in(adder_1_out), .out(transistor_1_out), .gate(not_1_out));
  Adder adder_1 (.a(tsb_2_o0), .b(tsb_3_o0), .out(adder_1_out), .cin(register_1_q[1]), .cout(nor_1_out[1]));
  Subtractor subtractor_1 (
    .a(tsb_2_o0), .b(tsb_3_o0), .out(subtractor_1_out), .bin(register_1_q[1]), .bout(nor_1_out[1]));
  Transistor #(.\type ("n"), .width(8)) transistor_2 (
    .in(subtractor_1_out), .out(transistor_1_out), .gate(R3_Control_Signals_sw1));
  Register register_1 (.D(nor_1_out), .clk(button_1_out), .Q(register_1_q));  // open: en, clr
  Register register_2 (.D(transistor_1_out), .clk(button_1_out), .Q(register_2_q));  // open: en, clr
  not not_1 (not_1_out, R3_Control_Signals_sw1);
endmodule

module TSB (
  input  I0,
  input  I1,
  input  I2,
  input  I3,
  input  I4,
  input  I5,
  input  I6,
  input  I7,
  input  OUT,
  input  OUT_2,
  output O0,
  output O1,
  output O2,
  output O3,
  output O4,
  output O5,
  output O6,
  output O6_2
);

  assign O0 = OUT ? I0 : 1'bz;  // Controlled_Buffer controlled_buffer_1
  assign O1 = OUT ? I1 : 1'bz;  // Controlled_Buffer controlled_buffer_2
  assign O3 = OUT ? I3 : 1'bz;  // Controlled_Buffer controlled_buffer_3
  assign O2 = OUT ? I2 : 1'bz;  // Controlled_Buffer controlled_buffer_4
  assign O5 = OUT ? I5 : 1'bz;  // Controlled_Buffer controlled_buffer_5
  assign O4 = OUT ? I4 : 1'bz;  // Controlled_Buffer controlled_buffer_6
  assign O6 = OUT ? I6 : 1'bz;  // Controlled_Buffer controlled_buffer_7
  assign O6_2 = OUT ? I7 : 1'bz;  // Controlled_Buffer controlled_buffer_8

  assign OUT_2 = OUT;
endmodule
