// Logisim project Floppy Disk Controller.circ as structural Verilog: 2 circuits, main circuit main
module main (
);

  wire and_1_out, and_2_out, and_3_out, and_4_out, and_5_out, and_6_out, and_7_out, and_8_out, and_9_out,
       button_1_out, dipswitch_1_sw1, dipswitch_1_sw2, dipswitch_1_sw3, dipswitch_1_sw4, dipswitch_1_sw5,
       dipswitch_1_sw6, dipswitch_1_sw7, dipswitch_1_sw8, dipswitch_2_sw1, dipswitch_2_sw2, dipswitch_2_sw3,
       dipswitch_2_sw4, dipswitch_2_sw5, dipswitch_2_sw6, dipswitch_2_sw7, dipswitch_2_sw8, dipswitch_3_sw1,
       dipswitch_3_sw2, dipswitch_3_sw3, dipswitch_3_sw4, dipswitch_3_sw5, dipswitch_3_sw6, dipswitch_3_sw7,
       dipswitch_3_sw8, not_1_out, not_2_out, not_3_out, not_4_out, not_5_out, not_6_out, not_7_out,
       not_8_out, not_9_out, not_10_out, not_11_out, not_12_out, not_13_out, not_14_out, not_15_out,
       not_16_out, pull_resistor_18_node, pull_resistor_19_node, pull_resistor_27_node, transistor_1_out,
       transistor_2_out, transistor_3_out, transistor_4_out, transistor_5_out, transistor_6_out,
       transistor_7_out, transistor_8_out, transistor_9_out, transistor_10_out, transistor_11_out,
       transistor_12_out, transistor_13_out, transistor_14_out, transistor_15_out, transistor_16_out,
       tsb_2_o0, tsb_2_o1, tsb_2_o2, tsb_2_o3, tsb_2_o4, tsb_2_o5, tsb_2_o6, tsb_2_o7;
  wire [7:0] pull_resistor_24_node, register_1_q, register_2_q, register_3_q, rom_1_data, tsb_1_o7;

  DipSwitch dipswitch_1 (
    .sw1(dipswitch_1_sw1), .sw2(dipswitch_1_sw2), .sw3(dipswitch_1_sw3), .sw4(dipswitch_1_sw4),
    .sw5(dipswitch_1_sw5), .sw6(dipswitch_1_sw6), .sw7(dipswitch_1_sw7), .sw8(dipswitch_1_sw8));
  DotMatrix #(.matrixcols(8), .matrixrows(1)) dotmatrix_1 (
    .col0(tsb_2_o7), .col1(tsb_2_o6), .col2(tsb_2_o5), .col3(tsb_2_o4), .col4(tsb_2_o3), .col5(tsb_2_o2),
    .col6(tsb_2_o1), .col7(tsb_2_o0));
  DipSwitch dipswitch_2 (
    .sw1(dipswitch_2_sw1), .sw2(dipswitch_2_sw2), .sw3(dipswitch_2_sw3), .sw4(dipswitch_2_sw4),
    .sw5(dipswitch_2_sw5), .sw6(dipswitch_2_sw6), .sw7(dipswitch_2_sw7), .sw8(dipswitch_2_sw8));
  DipSwitch dipswitch_3 (
    .sw1(dipswitch_3_sw1), .sw2(dipswitch_3_sw2), .sw3(dipswitch_3_sw3), .sw4(dipswitch_3_sw4),
    .sw5(dipswitch_3_sw5), .sw6(dipswitch_3_sw6), .sw7(dipswitch_3_sw7), .sw8(dipswitch_3_sw8));
  not not_1 (not_1_out, dipswitch_1_sw1);
  Transistor #(.\type ("n")) transistor_1 (.in(1'b1), .out(transistor_1_out), .gate(not_1_out));
  Transistor #(.\type ("n")) transistor_2 (.in(1'b1), .out(transistor_2_out), .gate(dipswitch_1_sw2));
  not not_2 (not_2_out, dipswitch_1_sw3);
  Transistor #(.\type ("n")) transistor_3 (.in(1'b1), .out(transistor_3_out), .gate(not_2_out));
  Transistor #(.\type ("n")) transistor_4 (.in(1'b1), .out(transistor_4_out), .gate(dipswitch_1_sw4));
  not not_3 (not_3_out, dipswitch_1_sw5);
  Transistor #(.\type ("n")) transistor_5 (.in(1'b1), .out(transistor_5_out), .gate(not_3_out));
  not not_4 (not_4_out, dipswitch_1_sw6);
  Transistor #(.\type ("n")) transistor_6 (.in(1'b1), .out(transistor_6_out), .gate(not_4_out));
  Transistor #(.\type ("n")) transistor_7 (.in(1'b1), .out(transistor_7_out), .gate(dipswitch_1_sw7));
  not not_5 (not_5_out, dipswitch_1_sw8);
  Transistor #(.\type ("n")) transistor_8 (.in(1'b1), .out(transistor_8_out), .gate(not_5_out));
  Button button_1 (.out(button_1_out));
  Pull_Resistor pull_resistor_1 (.node(transistor_2_out));
  Pull_Resistor pull_resistor_2 (.node(transistor_3_out));
  Pull_Resistor pull_resistor_3 (.node(transistor_1_out));
  Pull_Resistor pull_resistor_4 (.node(transistor_4_out));
  Pull_Resistor pull_resistor_5 (.node(transistor_7_out));
  Pull_Resistor pull_resistor_6 (.node(transistor_5_out));
  Pull_Resistor pull_resistor_7 (.node(transistor_6_out));
  Pull_Resistor pull_resistor_8 (.node(transistor_8_out));
  TSB tsb_1 (
    .O0(tsb_1_o7[7]), .O1(tsb_1_o7[6]), .O2(tsb_1_o7[5]), .O3(tsb_1_o7[4]), .O4(tsb_1_o7[3]),
    .O5(tsb_1_o7[2]), .O6(tsb_1_o7[1]), .O7(tsb_1_o7[0]), .I0(dipswitch_3_sw1), .I1(dipswitch_3_sw2),
    .I2(dipswitch_3_sw3), .I3(dipswitch_3_sw4), .I4(dipswitch_3_sw5), .I5(dipswitch_3_sw6),
    .I6(dipswitch_3_sw7), .I7(dipswitch_3_sw8), .OUT_2(not_6_out));  // open: OUT
  not not_6 (not_6_out, and_7_out);
  TSB tsb_2 (
    .O0(tsb_2_o0), .O1(tsb_2_o1), .O2(tsb_2_o2), .O3(tsb_2_o3), .O4(tsb_2_o4), .O5(tsb_2_o5), .O6(tsb_2_o6),
    .O7(tsb_2_o7), .I0(pull_resistor_24_node[0]), .I1(pull_resistor_24_node[1]),
    .I2(pull_resistor_24_node[2]), .I3(pull_resistor_24_node[3]), .I4(pull_resistor_24_node[4]),
    .I5(pull_resistor_24_node[5]), .I6(pull_resistor_24_node[6]), .I7(pull_resistor_24_node[7]),
    .OUT_2(and_7_out));  // open: OUT
  and and_1 (and_1_out, transistor_1_out, transistor_2_out, transistor_3_out, transistor_4_out, transistor_5_out, transistor_6_out, transistor_7_out, transistor_8_out);
  not not_7 (not_7_out, dipswitch_2_sw1);
  Transistor #(.\type ("n")) transistor_9 (.in(1'b1), .out(transistor_9_out), .gate(not_7_out));
  not not_8 (not_8_out, dipswitch_2_sw2);
  Transistor #(.\type ("n")) transistor_10 (.in(1'b1), .out(transistor_10_out), .gate(not_8_out));
  not not_9 (not_9_out, dipswitch_2_sw3);
  Transistor #(.\type ("n")) transistor_11 (.in(1'b1), .out(transistor_11_out), .gate(not_9_out));
  not not_10 (not_10_out, dipswitch_2_sw4);
  Transistor #(.\type ("n")) transistor_12 (.in(1'b1), .out(transistor_12_out), .gate(not_10_out));
  not not_11 (not_11_out, dipswitch_2_sw5);
  Transistor #(.\type ("n")) transistor_13 (.in(1'b1), .out(transistor_13_out), .gate(not_11_out));
  not not_12 (not_12_out, dipswitch_2_sw6);
  Transistor #(.\type ("n")) transistor_14 (.in(1'b1), .out(transistor_14_out), .gate(not_12_out));
  Pull_Resistor pull_resistor_9 (.node(pull_resistor_24_node[6]));
  Pull_Resistor pull_resistor_10 (.node(pull_resistor_24_node[5]));
  Pull_Resistor pull_resistor_11 (.node(pull_resistor_24_node[7]));
  Pull_Resistor pull_resistor_12 (.node(transistor_12_out));
  Pull_Resistor pull_resistor_13 (.node(transistor_10_out));
  Pull_Resistor pull_resistor_14 (.node(transistor_11_out));
  Pull_Resistor pull_resistor_15 (.node(transistor_9_out));
  Pull_Resistor pull_resistor_16 (.node(transistor_14_out));
  Pull_Resistor pull_resistor_17 (.node(transistor_13_out));
  Pull_Resistor pull_resistor_18 (.node(pull_resistor_18_node));
  Pull_Resistor pull_resistor_19 (.node(pull_resistor_19_node));
  Transistor #(.\type ("n")) transistor_15 (.in(dipswitch_2_sw7), .out(transistor_15_out), .gate(and_3_out));
  Pull_Resistor pull_resistor_20 (.node(transistor_15_out));
  Transistor #(.\type ("n")) transistor_16 (.in(dipswitch_2_sw8), .out(transistor_16_out), .gate(and_3_out));
  Pull_Resistor pull_resistor_21 (.node(transistor_16_out));
  Pull_Resistor pull_resistor_22 (.node(pull_resistor_24_node[2]));
  Pull_Resistor pull_resistor_23 (.node(pull_resistor_24_node[4]));
  Pull_Resistor pull_resistor_24 (.node(pull_resistor_24_node[0]));
  Pull_Resistor pull_resistor_25 (.node(pull_resistor_24_node[1]));
  Pull_Resistor pull_resistor_26 (.node(pull_resistor_24_node[3]));
  and and_2 (and_2_out, transistor_9_out, transistor_10_out, transistor_11_out, transistor_12_out, transistor_13_out, transistor_14_out, pull_resistor_18_node, pull_resistor_19_node);
  and and_3 (and_3_out, and_2_out, and_1_out);
  not not_13 (not_13_out, transistor_15_out);
  and and_4 (and_4_out, not_13_out, not_14_out);
  not not_14 (not_14_out, transistor_16_out);
  not not_15 (not_15_out, transistor_15_out);
  and and_5 (and_5_out, not_15_out, transistor_16_out);
  and and_6 (and_6_out, transistor_15_out, not_16_out);
  not not_16 (not_16_out, transistor_16_out);
  and and_7 (and_7_out, transistor_15_out, transistor_16_out);
  Register register_1 (.D(tsb_1_o7), .en(pull_resistor_27_node), .clk(and_8_out), .Q(register_1_q));  // open: clr
  Pull_Resistor pull_resistor_27 (.node(pull_resistor_27_node));
  Transistor #(.\type ("n")) transistor_17 (.in(and_4_out), .out(pull_resistor_27_node), .gate(and_3_out));
  Register register_2 (.D(tsb_1_o7), .en(and_5_out), .clk(and_8_out), .Q(register_2_q));  // open: clr
  Register register_3 (.D(tsb_1_o7), .en(and_6_out), .clk(and_8_out), .Q(register_3_q));  // open: clr
  and and_8 (and_8_out, and_3_out, button_1_out);
  Register register_4 (.D(rom_1_data), .clk(and_9_out), .Q(pull_resistor_24_node));  // open: en, clr
  and and_9 (and_9_out, button_1_out, and_7_out);
  ROM #(.addrWidth(24)) rom_1 (.addr({register_1_q, register_2_q, register_3_q}), .data(rom_1_data));
  // also tied to VCC on the sheet: {pull_resistor_18_node, pull_resistor_19_node}

  // Notes on the sheet:
  //   contents of rom_1 (hex, n*v repeats v):
  //   de ad be ef 20988*0 3 5 9 10
endmodule

module TSB (
  input  I0,
  input  I1,
  input  I2,
  input  I3,
  input  I4,
  input  I5,
  input  I6,
  input  I7,
  input  OUT,
  input  OUT_2,
  output O0,
  output O1,
  output O2,
  output O3,
  output O4,
  output O5,
  output O6,
  output O7
);

  assign O0 = OUT ? I0 : 1'bz;  // Controlled_Buffer controlled_buffer_1
  assign O2 = OUT ? I2 : 1'bz;  // Controlled_Buffer controlled_buffer_2
  assign O1 = OUT ? I1 : 1'bz;  // Controlled_Buffer controlled_buffer_3
  assign O3 = OUT ? I3 : 1'bz;  // Controlled_Buffer controlled_buffer_4
  assign O5 = OUT ? I5 : 1'bz;  // Controlled_Buffer controlled_buffer_5
  assign O4 = OUT ? I4 : 1'bz;  // Controlled_Buffer controlled_buffer_6
  assign O7 = OUT ? I7 : 1'bz;  // Controlled_Buffer controlled_buffer_7
  assign O6 = OUT ? I6 : 1'bz;  // Controlled_Buffer controlled_buffer_8

  assign OUT_2 = OUT;
endmodule
