// Logisim project Instruction Register.circ as structural Verilog: 2 circuits, main circuit main
module main (
);

  wire button_1_out, dipswitch_1_sw1, dipswitch_1_sw2, dipswitch_1_sw3, dipswitch_1_sw4, dipswitch_1_sw5,
       dipswitch_1_sw6, dipswitch_1_sw7, dipswitch_1_sw8, dipswitch_2_sw1, dipswitch_2_sw2, tsb_2_o0,
       tsb_2_o1, tsb_2_o2, tsb_2_o3, tsb_2_o4, tsb_2_o5, tsb_2_o6, tsb_2_o7;
  wire [7:0] pull_resistor_2_node, register_1_q;

  Pull_Resistor pull_resistor_1 (.node(pull_resistor_2_node[1]));
  Pull_Resistor pull_resistor_2 (.node(pull_resistor_2_node[0]));
  Pull_Resistor pull_resistor_3 (.node(pull_resistor_2_node[2]));
  Pull_Resistor pull_resistor_4 (.node(pull_resistor_2_node[4]));
  Pull_Resistor pull_resistor_5 (.node(pull_resistor_2_node[3]));
  Register register_1 (.D(pull_resistor_2_node), .clk(dipswitch_2_sw2), .Q(register_1_q));  // open: en, clr
  Pull_Resistor pull_resistor_6 (.node(pull_resistor_2_node[6]));
  TSB tsb_1 (
    .O0(pull_resistor_2_node[7]), .O1(pull_resistor_2_node[6]), .O2(pull_resistor_2_node[5]),
    .O3(pull_resistor_2_node[4]), .O4(pull_resistor_2_node[3]), .O5(pull_resistor_2_node[2]),
    .O6(pull_resistor_2_node[1]), .O7(pull_resistor_2_node[0]), .I0(dipswitch_1_sw1), .I1(dipswitch_1_sw2),
    .I2(dipswitch_1_sw3), .I3(dipswitch_1_sw4), .I4(dipswitch_1_sw5), .I5(dipswitch_1_sw6),
    .I6(dipswitch_1_sw7), .I7(dipswitch_1_sw8), .OUT_2(dipswitch_2_sw1));  // open: OUT
  Pull_Resistor pull_resistor_7 (.node(pull_resistor_2_node[5]));
  Pull_Resistor pull_resistor_8 (.node(pull_resistor_2_node[7]));
  TSB tsb_2 (
    .O0(tsb_2_o0), .O1(tsb_2_o1), .O2(tsb_2_o2), .O3(tsb_2_o3), .O4(tsb_2_o4), .O5(tsb_2_o5), .O6(tsb_2_o6),
    .O7(tsb_2_o7), .I0(register_1_q[0]), .I1(register_1_q[1]), .I2(register_1_q[2]), .I3(register_1_q[3]),
    .I4(register_1_q[4]), .I5(register_1_q[5]), .I6(register_1_q[6]), .I7(register_1_q[7]),
    .OUT_2(button_1_out));  // open: OUT
  DotMatrix #(.matrixcols(8), .matrixrows(1)) dotmatrix_1 (
    .col0(tsb_2_o7), .col1(tsb_2_o6), .col2(tsb_2_o5), .col3(tsb_2_o4), .col4(tsb_2_o3), .col5(tsb_2_o2),
    .col6(tsb_2_o1), .col7(tsb_2_o0));
  DipSwitch dipswitch_1 (
    .sw1(dipswitch_1_sw1), .sw2(dipswitch_1_sw2), .sw3(dipswitch_1_sw3), .sw4(dipswitch_1_sw4),
    .sw5(dipswitch_1_sw5), .sw6(dipswitch_1_sw6), .sw7(dipswitch_1_sw7), .sw8(dipswitch_1_sw8));
  DipSwitch dipswitch_2 (.sw1(dipswitch_2_sw1), .sw2(dipswitch_2_sw2));  // open: sw3, sw4, sw5, sw6, sw7, sw8
  Button button_1 (.out(button_1_out));
endmodule

module TSB (
  input  I0,
  input  I1,
  input  I2,
  input  I3,
  input  I4,
  input  I5,
  input  I6,
  input  I7,
  input  OUT,
  input  OUT_2,
  output O0,
  output O1,
  output O2,
  output O3,
  output O4,
  output O5,
  output O6,
  output O7
);

  assign O0 = OUT ? I0 : 1'bz;  // Controlled_Buffer controlled_buffer_1
  assign O1 = OUT ? I1 : 1'bz;  // Controlled_Buffer controlled_buffer_2
  assign O2 = OUT ? I2 : 1'bz;  // Controlled_Buffer controlled_buffer_3
  assign O3 = OUT ? I3 : 1'bz;  // Controlled_Buffer controlled_buffer_4
  assign O4 = OUT ? I4 : 1'bz;  // Controlled_Buffer controlled_buffer_5
  assign O5 = OUT ? I5 : 1'bz;  // Controlled_Buffer controlled_buffer_6
  assign O6 = OUT ? I6 : 1'bz;  // Controlled_Buffer controlled_buffer_7
  assign O7 = OUT ? I7 : 1'bz;  // Controlled_Buffer controlled_buffer_8

  assign OUT_2 = OUT;
endmodule
