// Logisim project Register.circ as structural Verilog: 2 circuits, main circuit main
module main (
);

  wire CLK_out, controlled_buffer_1_out, dipswitch_1_sw1, dipswitch_1_sw2, dipswitch_1_sw3, dipswitch_1_sw4,
       dipswitch_1_sw5, dipswitch_1_sw6, dipswitch_1_sw7, dipswitch_1_sw8, dipswitch_2_sw1, dipswitch_2_sw2,
       dipswitch_2_sw3, dipswitch_2_sw4, nand_1_out, nand_2_out, nand_3_out, nand_4_out, nand_5_out,
       nand_6_out, nand_7_out, nand_8_out, nand_9_out, nand_10_out, nand_11_out, nand_12_out, nand_13_out,
       nand_14_out, nand_15_out, nand_16_out, nand_17_out, nand_18_out, nand_19_out, nand_20_out,
       nand_21_out, nand_22_out, nand_23_out, nand_24_out, nand_25_out, nand_26_out, nand_27_out,
       nand_28_out, nand_29_out, nand_30_out, nand_31_out, nand_32_out, not_1_out, not_2_out, not_3_out,
       not_4_out, not_5_out, not_6_out, not_7_out, not_8_out, tsb_1_o0, tsb_1_o0_2, tsb_1_o0_3, tsb_1_o0_4,
       tsb_1_o0_5, tsb_1_o0_6, tsb_1_o0_7, tsb_1_o0_8, tsb_2_o0, tsb_2_o0_2, tsb_2_o0_3, tsb_2_o0_4,
       tsb_2_o0_5, tsb_2_o0_6, tsb_2_o0_7, tsb_2_o0_8, tsb_4_o0, tsb_4_o0_2, tsb_4_o0_3, tsb_4_o0_4,
       tsb_4_o0_5, tsb_4_o0_6, tsb_4_o0_7, tsb_4_o0_8;

  DotMatrix #(.matrixcols(8), .matrixrows(1)) dotmatrix_1 (
    .col0(tsb_1_o0), .col1(tsb_1_o0_2), .col2(tsb_1_o0_3), .col3(tsb_1_o0_4), .col4(tsb_1_o0_5),
    .col5(tsb_1_o0_6), .col6(tsb_1_o0_7), .col7(tsb_1_o0_8));
  DipSwitch dipswitch_1 (
    .sw1(dipswitch_1_sw1), .sw2(dipswitch_1_sw2), .sw3(dipswitch_1_sw3), .sw4(dipswitch_1_sw4),
    .sw5(dipswitch_1_sw5), .sw6(dipswitch_1_sw6), .sw7(dipswitch_1_sw7), .sw8(dipswitch_1_sw8));
  TSB tsb_1 (
    .O0(tsb_1_o0), .O0_2(tsb_1_o0_2), .O0_3(tsb_1_o0_3), .O0_4(tsb_1_o0_4), .O0_5(tsb_1_o0_5),
    .O0_6(tsb_1_o0_6), .O0_7(tsb_1_o0_7), .O0_8(tsb_1_o0_8), .I0(dipswitch_1_sw1), .I0_2(dipswitch_1_sw2),
    .I0_3(dipswitch_1_sw3), .I0_4(dipswitch_1_sw4), .I0_5(dipswitch_1_sw5), .I0_6(dipswitch_1_sw6),
    .I0_7(dipswitch_1_sw7), .I0_8(dipswitch_1_sw8), .OUT_2(dipswitch_2_sw1));  // open: OUT
  TSB tsb_2 (
    .O0(tsb_2_o0), .O0_2(tsb_2_o0_2), .O0_3(tsb_2_o0_3), .O0_4(tsb_2_o0_4), .O0_5(tsb_2_o0_5),
    .O0_6(tsb_2_o0_6), .O0_7(tsb_2_o0_7), .O0_8(tsb_2_o0_8), .I0(tsb_1_o0), .I0_2(tsb_1_o0_2),
    .I0_3(tsb_1_o0_3), .I0_4(tsb_1_o0_4), .I0_5(tsb_1_o0_5), .I0_6(tsb_1_o0_6), .I0_7(tsb_1_o0_7),
    .I0_8(tsb_1_o0_8), .OUT_2(dipswitch_2_sw2));  // open: OUT
  TSB tsb_3 (
    .OUT(dipswitch_2_sw3), .O0(tsb_1_o0), .O0_2(tsb_1_o0_2), .O0_3(tsb_1_o0_3), .O0_4(tsb_1_o0_4),
    .O0_5(tsb_1_o0_5), .O0_6(tsb_1_o0_6), .O0_7(tsb_1_o0_7), .O0_8(tsb_1_o0_8), .I0(nand_17_out),
    .I0_2(nand_19_out), .I0_3(nand_21_out), .I0_4(nand_23_out), .I0_5(nand_25_out), .I0_6(nand_27_out),
    .I0_7(nand_29_out), .I0_8(nand_31_out));  // open: OUT_2
  DipSwitch dipswitch_2 (
    .sw1(dipswitch_2_sw1), .sw2(dipswitch_2_sw2), .sw3(dipswitch_2_sw3), .sw4(dipswitch_2_sw4));  // open: sw5, sw6, sw7, sw8
  assign controlled_buffer_1_out = CLK_out ? CLK_out : 1'bz;  // Controlled_Buffer controlled_buffer_1
  Button CLK (.out(CLK_out));
  Pull_Resistor pull_resistor_1 (.node(tsb_2_o0));
  not not_1 (not_1_out, tsb_2_o0);
  Pull_Resistor pull_resistor_2 (.node(tsb_2_o0_2));
  not not_2 (not_2_out, tsb_2_o0_2);
  Pull_Resistor pull_resistor_3 (.node(tsb_2_o0_3));
  not not_3 (not_3_out, tsb_2_o0_3);
  Pull_Resistor pull_resistor_4 (.node(tsb_2_o0_4));
  not not_4 (not_4_out, tsb_2_o0_4);
  Pull_Resistor pull_resistor_5 (.node(tsb_2_o0_5));
  not not_5 (not_5_out, tsb_2_o0_5);
  Pull_Resistor pull_resistor_6 (.node(tsb_2_o0_6));
  not not_6 (not_6_out, tsb_2_o0_6);
  Pull_Resistor pull_resistor_7 (.node(tsb_2_o0_7));
  not not_7 (not_7_out, tsb_2_o0_7);
  Pull_Resistor pull_resistor_8 (.node(tsb_2_o0_8));
  not not_8 (not_8_out, tsb_2_o0_8);
  nand nand_1 (nand_1_out, tsb_2_o0, controlled_buffer_1_out);
  nand nand_2 (nand_2_out, controlled_buffer_1_out, not_1_out);
  nand nand_3 (nand_3_out, tsb_2_o0_2, controlled_buffer_1_out);
  nand nand_4 (nand_4_out, controlled_buffer_1_out, not_2_out);
  nand nand_5 (nand_5_out, tsb_2_o0_3, controlled_buffer_1_out);
  nand nand_6 (nand_6_out, controlled_buffer_1_out, not_3_out);
  nand nand_7 (nand_7_out, tsb_2_o0_4, controlled_buffer_1_out);
  nand nand_8 (nand_8_out, controlled_buffer_1_out, not_4_out);
  nand nand_9 (nand_9_out, tsb_2_o0_5, controlled_buffer_1_out);
  nand nand_10 (nand_10_out, controlled_buffer_1_out, not_5_out);
  nand nand_11 (nand_11_out, tsb_2_o0_6, controlled_buffer_1_out);
  nand nand_12 (nand_12_out, controlled_buffer_1_out, not_6_out);
  nand nand_13 (nand_13_out, tsb_2_o0_7, controlled_buffer_1_out);
  nand nand_14 (nand_14_out, controlled_buffer_1_out, not_7_out);
  nand nand_15 (nand_15_out, tsb_2_o0_8, controlled_buffer_1_out);
  nand nand_16 (nand_16_out, controlled_buffer_1_out, not_8_out);
  nand nand_17 (nand_17_out, nand_1_out, nand_18_out);
  nand nand_18 (nand_18_out, nand_17_out, nand_2_out);
  nand nand_19 (nand_19_out, nand_3_out, nand_20_out);
  nand nand_20 (nand_20_out, nand_19_out, nand_4_out);
  nand nand_21 (nand_21_out, nand_5_out, nand_22_out);
  nand nand_22 (nand_22_out, nand_21_out, nand_6_out);
  nand nand_23 (nand_23_out, nand_7_out, nand_24_out);
  nand nand_24 (nand_24_out, nand_23_out, nand_8_out);
  nand nand_25 (nand_25_out, nand_9_out, nand_26_out);
  nand nand_26 (nand_26_out, nand_25_out, nand_10_out);
  nand nand_27 (nand_27_out, nand_11_out, nand_28_out);
  nand nand_28 (nand_28_out, nand_27_out, nand_12_out);
  nand nand_29 (nand_29_out, nand_13_out, nand_30_out);
  nand nand_30 (nand_30_out, nand_29_out, nand_14_out);
  nand nand_31 (nand_31_out, nand_15_out, nand_32_out);
  nand nand_32 (nand_32_out, nand_31_out, nand_16_out);
  TSB tsb_4 (
    .O0(tsb_4_o0), .O0_2(tsb_4_o0_2), .O0_3(tsb_4_o0_3), .O0_4(tsb_4_o0_4), .O0_5(tsb_4_o0_5),
    .O0_6(tsb_4_o0_6), .O0_7(tsb_4_o0_7), .O0_8(tsb_4_o0_8), .I0(nand_17_out), .I0_2(nand_19_out),
    .I0_3(nand_21_out), .I0_4(nand_23_out), .I0_5(nand_25_out), .I0_6(nand_27_out), .I0_7(nand_29_out),
    .I0_8(nand_31_out), .OUT_2(dipswitch_2_sw4));  // open: OUT
  // RGBLED rgbled_1: pin names not known

  // Notes on the sheet:
  //   1= Bus Out
  //   2= Reg in
  //   3= Reg ->Bus
  //   4= Reg -> Acc
endmodule

module TSB (
  input  I0,
  input  I0_2,
  input  I0_3,
  input  I0_4,
  input  I0_5,
  input  I0_6,
  input  I0_7,
  input  I0_8,
  input  OUT,
  input  OUT_2,
  output O0,
  output O0_2,
  output O0_3,
  output O0_4,
  output O0_5,
  output O0_6,
  output O0_7,
  output O0_8
);

  assign O0 = OUT ? I0 : 1'bz;  // Controlled_Buffer controlled_buffer_1
  assign O0_3 = OUT ? I0_3 : 1'bz;  // Controlled_Buffer controlled_buffer_2
  assign O0_2 = OUT ? I0_2 : 1'bz;  // Controlled_Buffer controlled_buffer_3
  assign O0_4 = OUT ? I0_4 : 1'bz;  // Controlled_Buffer controlled_buffer_4
  assign O0_5 = OUT ? I0_5 : 1'bz;  // Controlled_Buffer controlled_buffer_5
  assign O0_6 = OUT ? I0_6 : 1'bz;  // Controlled_Buffer controlled_buffer_6
  assign O0_7 = OUT ? I0_7 : 1'bz;  // Controlled_Buffer controlled_buffer_7
  assign O0_8 = OUT ? I0_8 : 1'bz;  // Controlled_Buffer controlled_buffer_8

  assign OUT_2 = OUT;
endmodule
