// Logisim project Wilson-1 clock.circ as structural Verilog: 1 circuit, main circuit main
module main (
);

  wire CLK, clock_1_out, RUN, STEP;

  Pull_Resistor pull_resistor_1 (.node(CLK));
  Clock clock_1 (.out(clock_1_out));
  Transistor #(.\type ("n"), .gate("br")) transistor_1 (.in(1'b1), .out(CLK), .gate(STEP));
  DipSwitch dipswitch_1 (.sw1(RUN));  // open: sw2, sw3, sw4, sw5, sw6, sw7, sw8
  Button button_1 (.out(STEP));
  Transistor #(.\type ("n")) transistor_2 (.in(RUN), .out(CLK), .gate(clock_1_out));

  // Notes on the sheet:
  //   Transistors met label N niet nodig
  //   N
endmodule
