// Logisim project memory.circ as structural Verilog: 3 circuits, main circuit main
module main (
);

  wire clock_1_out, controlled_buffer_1_out, controlled_buffer_2_out, dipswitch_1_sw1, dipswitch_1_sw2,
       dipswitch_1_sw3, dipswitch_1_sw4, dipswitch_1_sw5, dipswitch_1_sw6, dipswitch_1_sw7, dipswitch_1_sw8,
       dipswitch_2_sw1, dipswitch_2_sw2, dipswitch_2_sw3, dipswitch_2_sw4, dipswitch_2_sw5;
  wire [7:0] mar_1_o0, ram_1_data, tristatebuffer_1_o7;

  MAR mar_1 (
    .O0(mar_1_o0[0]), .O1(mar_1_o0[1]), .O2(mar_1_o0[2]), .O3(mar_1_o0[3]), .O4(mar_1_o0[4]),
    .O5(mar_1_o0[5]), .O6(mar_1_o0[6]), .out_18(mar_1_o0[7]), .I0(tristatebuffer_1_o7[0]),
    .I1(tristatebuffer_1_o7[1]), .I2(tristatebuffer_1_o7[2]), .I3(tristatebuffer_1_o7[3]),
    .I4(tristatebuffer_1_o7[4]), .I5(tristatebuffer_1_o7[5]), .I6(tristatebuffer_1_o7[6]),
    .O7(tristatebuffer_1_o7[7]), .MC(dipswitch_2_sw5), .MI(controlled_buffer_1_out));
  assign controlled_buffer_1_out = dipswitch_2_sw4 ? clock_1_out : 1'bz;  // Controlled_Buffer controlled_buffer_1
  assign controlled_buffer_2_out = dipswitch_2_sw2 ? clock_1_out : 1'bz;  // Controlled_Buffer controlled_buffer_2
  Clock clock_1 (.out(clock_1_out));
  RAM #(.bus("separate")) ram_1 (
    .addr(mar_1_o0), .din(tristatebuffer_1_o7), .data(ram_1_data), .clk(controlled_buffer_2_out));  // open: str, sel, ld, clr
  triStateBuffer tristatebuffer_1 (
    .O0(tristatebuffer_1_o7[7]), .O1(tristatebuffer_1_o7[6]), .O2(tristatebuffer_1_o7[5]),
    .O3(tristatebuffer_1_o7[4]), .O4(tristatebuffer_1_o7[3]), .O5(tristatebuffer_1_o7[2]),
    .O6(tristatebuffer_1_o7[1]), .O7(tristatebuffer_1_o7[0]), .I0(ram_1_data[7]), .I1(ram_1_data[6]),
    .I2(ram_1_data[5]), .I3(ram_1_data[4]), .I4(ram_1_data[3]), .I5(ram_1_data[2]), .I6(ram_1_data[1]),
    .I7(ram_1_data[0]), .OUT_2(dipswitch_2_sw3));  // open: OUT
  DotMatrix #(.matrixcols(8), .matrixrows(1)) dotmatrix_1 (
    .col0(tristatebuffer_1_o7[0]), .col1(tristatebuffer_1_o7[1]), .col2(tristatebuffer_1_o7[2]),
    .col3(tristatebuffer_1_o7[3]), .col4(tristatebuffer_1_o7[4]), .col5(tristatebuffer_1_o7[5]),
    .col6(tristatebuffer_1_o7[6]), .col7(tristatebuffer_1_o7[7]));
  DipSwitch dipswitch_1 (
    .sw1(dipswitch_1_sw1), .sw2(dipswitch_1_sw2), .sw3(dipswitch_1_sw3), .sw4(dipswitch_1_sw4),
    .sw5(dipswitch_1_sw5), .sw6(dipswitch_1_sw6), .sw7(dipswitch_1_sw7), .sw8(dipswitch_1_sw8));
  triStateBuffer tristatebuffer_2 (
    .O0(tristatebuffer_1_o7[0]), .O1(tristatebuffer_1_o7[1]), .O2(tristatebuffer_1_o7[2]),
    .O3(tristatebuffer_1_o7[3]), .O4(tristatebuffer_1_o7[4]), .O5(tristatebuffer_1_o7[5]),
    .O6(tristatebuffer_1_o7[6]), .O7(tristatebuffer_1_o7[7]), .I0(dipswitch_1_sw1), .I1(dipswitch_1_sw2),
    .I2(dipswitch_1_sw3), .I3(dipswitch_1_sw4), .I4(dipswitch_1_sw5), .I5(dipswitch_1_sw6),
    .I6(dipswitch_1_sw7), .I7(dipswitch_1_sw8), .OUT_2(dipswitch_2_sw1));  // open: OUT
  DipSwitch dipswitch_2 (
    .sw1(dipswitch_2_sw1), .sw2(dipswitch_2_sw2), .sw3(dipswitch_2_sw3), .sw4(dipswitch_2_sw4),
    .sw5(dipswitch_2_sw5));  // open: sw6, sw7, sw8

  // Notes on the sheet:
  //   Memory Address Register
  //   BUS IN
  //   Ram IN
  //   Ram OUT
  //   MAR IN
  //   MAR CLR
endmodule

module triStateBuffer (
  input  I0,
  input  I1,
  input  I2,
  input  I3,
  input  I4,
  input  I5,
  input  I6,
  input  I7,
  input  OUT,
  input  OUT_2,
  output O0,
  output O1,
  output O2,
  output O3,
  output O4,
  output O5,
  output O6,
  output O7
);

  assign O0 = OUT ? I0 : 1'bz;  // Controlled_Buffer controlled_buffer_1
  assign O1 = OUT ? I1 : 1'bz;  // Controlled_Buffer controlled_buffer_2
  assign O2 = OUT ? I2 : 1'bz;  // Controlled_Buffer controlled_buffer_3
  assign O3 = OUT ? I3 : 1'bz;  // Controlled_Buffer controlled_buffer_4
  assign O4 = OUT ? I4 : 1'bz;  // Controlled_Buffer controlled_buffer_5
  assign O5 = OUT ? I5 : 1'bz;  // Controlled_Buffer controlled_buffer_6
  assign O6 = OUT ? I6 : 1'bz;  // Controlled_Buffer controlled_buffer_7
  assign O7 = OUT ? I7 : 1'bz;  // Controlled_Buffer controlled_buffer_8

  assign OUT_2 = OUT;
endmodule

module MAR (
  input  MC,
  input  MI,
  input  I0,
  input  I1,
  input  I2,
  input  I3,
  input  I4,
  input  I5,
  input  I6,
  input  O7,
  output O0,
  output O1,
  output O2,
  output O3,
  output O4,
  output O5,
  output O6,
  output out_18
);

  D_Flip_Flop d_ff_1 (.D(I0), .clk(MI), .Q(O0), .reset(MC));  // open: Qn, preset
  D_Flip_Flop d_ff_2 (.D(I1), .clk(MI), .Q(O1), .reset(MC));  // open: Qn, preset
  D_Flip_Flop d_ff_3 (.D(I2), .clk(MI), .Q(O2), .reset(MC));  // open: Qn, preset
  D_Flip_Flop d_ff_4 (.D(I3), .clk(MI), .Q(O3), .reset(MC));  // open: Qn, preset
  D_Flip_Flop d_ff_5 (.D(I4), .clk(MI), .Q(O4), .reset(MC));  // open: Qn, preset
  D_Flip_Flop d_ff_6 (.D(I5), .clk(MI), .Q(O5), .reset(MC));  // open: Qn, preset
  D_Flip_Flop d_ff_7 (.D(I6), .clk(MI), .Q(O6), .reset(MC));  // open: Qn, preset
  D_Flip_Flop d_ff_8 (.D(O7), .clk(MI), .Q(out_18), .reset(MC));  // open: Qn, preset
endmodule
